# Fritzing sketch 1.7 Analog Input Control Output (saved by Fritzing 0.9.3b)
breadboards: 1

parts:
  元件1 = Arduino Mega ADK (Rev3)
  LED1 = LED - 5mm [color="Red (633nm)" package="5 mm [THT]"]
  R1 = Potentiometer [package=THT]
  R2 = Resistor [tolerance=±5% resistance=220 package=THT]

nets:
  N1: 元件1.A0, R1.wiper
  N2: 元件1.GND, LED1.cathode, R1.leg2
  N3: 元件1.D9_PWM, R2.Pin_1
  N4: 元件1.5V, R1.leg1
  N5: LED1.anode, R2.Pin_0

custom parts:
  Arduino Mega ADK (Rev3): The Arduino ADK is a microcontroller board based on the ATmega2560 (datasheet). It has a USB host interface to connect with Android based phones, based on the MAX3421e IC. It has 54 digital input/output pins (of which 14 can be used as PWM outputs), 16 analog inputs, 4 UARTs (hardware serial ports), a 16 MHz crystal oscillator, a USB connection, a power jack, an ICSP header, and a reset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
  Potentiometer: A standard adjustable resistor (potentiometer).
