# Fritzing sketch 2.13 Motor (saved by Fritzing 0.9.2b)
breadboards: 1

parts:
  元件1 = Arduino Mega ADK (Rev3)
  IC1 = Power Module V1.0 [package=THT]
  IC2 = L293D [package=THT]
  M1 = DC Motor

nets:
  N1: 元件1.GND, IC1.-#5, IC2.0V
  N2: 元件1.D10_PWM, IC2.In_1
  N3: 元件1.D9_PWM, IC2.In_2
  N4: IC1.+#2, IC2.+V
  N5: IC1.+#3, IC2.Enable_1, IC2.+Vmotor
  N6: IC2.Out_1_(_Controlled_by_Enable_1_), M1.pin_2
  N7: IC2.Out_2_(_Controlled_by_Enable_1_), M1.pin_1

custom parts:
  Arduino Mega ADK (Rev3): The Arduino ADK is a microcontroller board based on the ATmega2560 (datasheet). It has a USB host interface to connect with Android based phones, based on the MAX3421e IC. It has 54 digital input/output pins (of which 14 can be used as PWM outputs), 16 analog inputs, 4 UARTs (hardware serial ports), a 16 MHz crystal oscillator, a USB connection, a power jack, an ICSP header, and a reset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
  Power Module V1.0: Power Module used for BreadBoard www.sunfounder.com
