# Fritzing sketch 2.14 Stepper Moto (saved by Fritzing 0.9.2b)
breadboards: 1

parts:
  元件1 = Arduino Mega ADK (Rev3)
  U1 = Stepper Motor Driver-v1.0 [package="DIP28 [THT]"]
  module1 = Step Motor
  IC1 = Power Module V1.0 [package=THT]

nets:
  N1: 元件1.GND, U1.-, IC1.-#5
  N2: 元件1.D2_PWM, 元件1.D3_PWM, 元件1.D4_PWM, 元件1.D5_PWM, U1.IN1, U1.IN2, U1.IN3, U1.IN4
  N3: U1.+, IC1.+#3
  N4: U1.OUT1, U1.OUT2, U1.OUT3, U1.OUT4, U1.COM, module1.yellow, module1.orange, module1.red, module1.pink, module1.blue

custom parts:
  Arduino Mega ADK (Rev3): The Arduino ADK is a microcontroller board based on the ATmega2560 (datasheet). It has a USB host interface to connect with Android based phones, based on the MAX3421e IC. It has 54 digital input/output pins (of which 14 can be used as PWM outputs), 16 analog inputs, 4 UARTs (hardware serial ports), a 16 MHz crystal oscillator, a USB connection, a power jack, an ICSP header, and a reset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
  Stepper Motor Driver-v1.0: Stepper Motor Driver
  Step Motor: step motor
  Power Module V1.0: Power Module used for BreadBoard www.sunfounder.com
