# Fritzing sketch 2.16 Switch (saved by Fritzing 0.9.3b)
breadboards: 1

parts:
  元件1 = Arduino Mega ADK (Rev3)
  S1 = Toggle Switch [package=THT]
  R1 = Resistor [tolerance=±5% resistance=10k package=THT]
  104 = Capacitor [package=cap-pth-small2]  # not connected

nets:
  N1: 元件1.5V, S1.L1
  N2: 元件1.GND, S1.L2, R1.Pin_0
  N3: 元件1.D2_PWM, S1.COM, R1.Pin_1

custom parts:
  Arduino Mega ADK (Rev3): The Arduino ADK is a microcontroller board based on the ATmega2560 (datasheet). It has a USB host interface to connect with Android based phones, based on the MAX3421e IC. It has 54 digital input/output pins (of which 14 can be used as PWM outputs), 16 analog inputs, 4 UARTs (hardware serial ports), a 16 MHz crystal oscillator, a USB connection, a power jack, an ICSP header, and a reset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
  Capacitor: Capacitor Standard 0603 ceramic capacitor, and 0.1 leaded capacitor.
