# Fritzing sketch 2.19 Keypad (saved by Fritzing 0.9.2b)

parts:
  元件1 = Arduino Mega ADK (Rev3)
  IC1 = 4*4 keyboard [chip_label=IC package="DIP (Dual Inline) [THT]"]

nets:
  N1: 元件1.D0/RX0, IC1.X1
  N2: 元件1.D1/TX0, IC1.X2
  N3: 元件1.D2_PWM, IC1.X3
  N4: 元件1.D3_PWM, IC1.X4
  N5: 元件1.D4_PWM, IC1.Y1
  N6: 元件1.D5_PWM, IC1.Y2
  N7: 元件1.D6_PWM, IC1.Y3
  N8: 元件1.D7_PWM, IC1.Y4

custom parts:
  Arduino Mega ADK (Rev3): The Arduino ADK is a microcontroller board based on the ATmega2560 (datasheet). It has a USB host interface to connect with Android based phones, based on the MAX3421e IC. It has 54 digital input/output pins (of which 14 can be used as PWM outputs), 16 analog inputs, 4 UARTs (hardware serial ports), a 16 MHz crystal oscillator, a USB connection, a power jack, an ICSP header, and a reset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
  4*4 keyboard: A 4*4 keyboard
