# Fritzing sketch 2.20 IR Remote (saved by Fritzing 0.9.2b)

parts:
  module1 = Ir Receiver-v1.0
  元件1 = Arduino Mega ADK (Rev3)

nets:
  N1: module1._, 元件1.GND
  N2: module1.+, 元件1.5V
  N3: module1.s, 元件1.D11_PWM

custom parts:
  Ir Receiver-v1.0: Infrared-Receiver module of SunFounder Sensor Kit
  Arduino Mega ADK (Rev3): The Arduino ADK is a microcontroller board based on the ATmega2560 (datasheet). It has a USB host interface to connect with Android based phones, based on the MAX3421e IC. It has 54 digital input/output pins (of which 14 can be used as PWM outputs), 16 analog inputs, 4 UARTs (hardware serial ports), a 16 MHz crystal oscillator, a USB connection, a power jack, an ICSP header, and a reset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
