# Fritzing sketch 2.21 Relay Module (saved by Fritzing 0.9.2b)
breadboards: 1

parts:
  元件1 = Arduino Mega ADK (Rev3)
  LED1 = LED - 5mm [color="Red (633nm)" package="5 mm [THT]"]
  R1 = Resistor [tolerance=±5% resistance=220 package=THT]
  IC1 = Power Module V1.0 [package=THT]
  U1 = 1PCS Relay Module [package=relay-g5q]

nets:
  N1: 元件1.GND, U1.-
  N2: 元件1.D9_PWM, U1.S
  N3: 元件1.5V, U1.+
  N4: LED1.cathode, IC1.-#5
  N5: LED1.anode, R1.Pin_1
  N6: R1.Pin_0, U1.NO
  N7: IC1.3.3V, IC1.-#4
  N8: IC1.+#2, IC1.GND
  N9: IC1.+#3, U1.COM

custom parts:
  Arduino Mega ADK (Rev3): The Arduino ADK is a microcontroller board based on the ATmega2560 (datasheet). It has a USB host interface to connect with Android based phones, based on the MAX3421e IC. It has 54 digital input/output pins (of which 14 can be used as PWM outputs), 16 analog inputs, 4 UARTs (hardware serial ports), a 16 MHz crystal oscillator, a USB connection, a power jack, an ICSP header, and a reset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
  Power Module V1.0: Power Module used for BreadBoard www.sunfounder.com
