# Fritzing sketch 2.22 Potentiometer (saved by Fritzing 0.9.2b)
breadboards: 1

parts:
  元件1 = Arduino Mega ADK (Rev3)
  R2 = Potentiometer [package=THT]

nets:
  N1: 元件1.A0, R2.wiper
  N2: 元件1.GND, R2.leg2
  N3: 元件1.5V, R2.leg1

custom parts:
  Arduino Mega ADK (Rev3): The Arduino ADK is a microcontroller board based on the ATmega2560 (datasheet). It has a USB host interface to connect with Android based phones, based on the MAX3421e IC. It has 54 digital input/output pins (of which 14 can be used as PWM outputs), 16 analog inputs, 4 UARTs (hardware serial ports), a 16 MHz crystal oscillator, a USB connection, a power jack, an ICSP header, and a reset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
  Potentiometer: A standard adjustable resistor (potentiometer).
