# Fritzing sketch 2.23 Joystick (saved by Fritzing 0.9.3b)

parts:
  元件1 = Arduino Mega ADK (Rev3)
  S1 = Joystick PS2 v1.0 [package=THT]

nets:
  N1: 元件1.A0, S1.VRX
  N2: 元件1.A1, S1.VRY
  GND: 元件1.GND, S1.GND
  N3: 元件1.D8_PWM, S1.SW
  5V: 元件1.5V, S1.VCC

custom parts:
  Arduino Mega ADK (Rev3): The Arduino ADK is a microcontroller board based on the ATmega2560 (datasheet). It has a USB host interface to connect with Android based phones, based on the MAX3421e IC. It has 54 digital input/output pins (of which 14 can be used as PWM outputs), 16 analog inputs, 4 UARTs (hardware serial ports), a 16 MHz crystal oscillator, a USB connection, a power jack, an ICSP header, and a reset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
  Joystick PS2 v1.0: A joystick is an input device consisting of a stick that pivots on a base and reports its angle or direction to the device it is controlling. Joysticks are often used to control video games and robots. A Joystick PS2 is used here.
