# Fritzing sketch 2.24 MPR121 (saved by Fritzing 0.9.3b)
breadboards: 1

parts:
  元件1 = Arduino Mega ADK (Rev3)
  元件2 = Electrodes/LEDs

nets:
  N1: 元件1.D21/SCL, 元件2.SCL
  N2: 元件1.D20/SDA, 元件2.SDA
  3V3: 元件1.3V3, 元件2.3.3V
  GND: 元件1.GND, 元件2.GND
  N3: 元件1.D2_PWM, 元件2.IRQ

custom parts:
  Arduino Mega ADK (Rev3): The Arduino ADK is a microcontroller board based on the ATmega2560 (datasheet). It has a USB host interface to connect with Android based phones, based on the MAX3421e IC. It has 54 digital input/output pins (of which 14 can be used as PWM outputs), 16 analog inputs, 4 UARTs (hardware serial ports), a 16 MHz crystal oscillator, a USB connection, a power jack, an ICSP header, and a reset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
  Electrodes/LEDs: The Arduino Ethernet is a microcontroller board based on the ATmega328 (datasheet). It has 14 digital input/output pins, 6 analog inputs, a 16 MHz crystal oscillator, a RJ45 connection, a power jack, an ICSP header, and a reset button. NB: Pins 10, 11, 12 and 13 are reserved for interfacing with the Ethernet module and should not be used otherwise. This reduces the number of available pins to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
