# Fritzing sketch 2.28 Sound Sensor Module (saved by Fritzing 0.9.3b)

parts:
  元件1 = IR Receiver
  元件2 = Arduino Mega ADK (Rev3)

nets:
  N1: 元件1.AO, 元件2.A0
  N2: 元件1.G, 元件2.GND
  N3: 元件1.+, 元件2.5V
  N4: 元件1.D0, 元件2.D2_PWM

custom parts:
  Arduino Mega ADK (Rev3): The Arduino ADK is a microcontroller board based on the ATmega2560 (datasheet). It has a USB host interface to connect with Android based phones, based on the MAX3421e IC. It has 54 digital input/output pins (of which 14 can be used as PWM outputs), 16 analog inputs, 4 UARTs (hardware serial ports), a 16 MHz crystal oscillator, a USB connection, a power jack, an ICSP header, and a reset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
