# Fritzing sketch 2.3 RGB LED (saved by Fritzing 0.9.3b)
breadboards: 1

parts:
  元件1 = Arduino Mega ADK (Rev3)
  R1 = Resistor [tolerance=±5% resistance=220 package=THT]
  LED1 = RGB LED (com. cathode, rgb) [package="5 mm [THT]"]
  R3 = Resistor [tolerance=±5% resistance=220 package=THT]
  R4 = Resistor [tolerance=±5% resistance=220 package=THT]

nets:
  N1: 元件1.GND, LED1.common_cathode
  N2: 元件1.D11_PWM, R4.Pin_1
  N3: 元件1.D10_PWM, R1.Pin_1
  N4: 元件1.D9_PWM, R3.Pin_1
  N5: R1.Pin_0, LED1.green_anode
  N6: LED1.red_anode, R4.Pin_0
  N7: LED1.blue_anode, R3.Pin_0

custom parts:
  Arduino Mega ADK (Rev3): The Arduino ADK is a microcontroller board based on the ATmega2560 (datasheet). It has a USB host interface to connect with Android based phones, based on the MAX3421e IC. It has 54 digital input/output pins (of which 14 can be used as PWM outputs), 16 analog inputs, 4 UARTs (hardware serial ports), a 16 MHz crystal oscillator, a USB connection, a power jack, an ICSP header, and a reset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
