# Fritzing sketch 2.33 Ultrasonic Module (saved by Fritzing 0.9.3b)

parts:
  元件1 = Arduino Mega ADK (Rev3)
  HC-SR04_Sensor_1 = HC-SR04 Ultrasonic Distance Sensor

nets:
  5V: 元件1.5V, HC-SR04_Sensor_1.VCC
  GND: 元件1.GND, HC-SR04_Sensor_1.GND
  N1: 元件1.D4_PWM, HC-SR04_Sensor_1.ECHO
  N2: 元件1.D5_PWM, HC-SR04_Sensor_1.TRIG

custom parts:
  Arduino Mega ADK (Rev3): The Arduino ADK is a microcontroller board based on the ATmega2560 (datasheet). It has a USB host interface to connect with Android based phones, based on the MAX3421e IC. It has 54 digital input/output pins (of which 14 can be used as PWM outputs), 16 analog inputs, 4 UARTs (hardware serial ports), a 16 MHz crystal oscillator, a USB connection, a power jack, an ICSP header, and a reset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
