# Fritzing sketch 2.34 MPU6050 (saved by Fritzing 0.9.3b)
breadboards: 1

parts:
  元件1 = Arduino Mega ADK (Rev3)
  module1 = MPU6050

nets:
  N1: 元件1.D21/SCL, module1.SCL
  N2: 元件1.D20/SDA, module1.SDA
  GND: 元件1.GND, module1.GND
  5V: 元件1.5V, module1.VCC

custom parts:
  Arduino Mega ADK (Rev3): The Arduino ADK is a microcontroller board based on the ATmega2560 (datasheet). It has a USB host interface to connect with Android based phones, based on the MAX3421e IC. It has 54 digital input/output pins (of which 14 can be used as PWM outputs), 16 analog inputs, 4 UARTs (hardware serial ports), a 16 MHz crystal oscillator, a USB connection, a power jack, an ICSP header, and a reset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
  MPU6050: MPU6050 Gyro Acceleration module of SunFounder Sensor Kit
