# Fritzing sketch 2.35 RFID (saved by Fritzing 0.9.3b)

parts:
  module2 = RFID-RC522-blue
  元件1 = Arduino Mega ADK (Rev3)

nets:
  3.3V: module2.3.3V, 元件1.3V3
  N1: module2.RST, 元件1.D2_PWM
  GND: module2.GND, 元件1.GND
  N2: module2.MISO, 元件1.D3_PWM
  N3: module2.MOSI, 元件1.D4_PWM
  N4: module2.SCK, 元件1.D5_PWM
  N5: module2.SDA, 元件1.D6_PWM
  N6: module2.IRQ, 元件1.D7_PWM

custom parts:
  RFID-RC522-blue: RFID-RC522 module from Sunfounder
  Arduino Mega ADK (Rev3): The Arduino ADK is a microcontroller board based on the ATmega2560 (datasheet). It has a USB host interface to connect with Android based phones, based on the MAX3421e IC. It has 54 digital input/output pins (of which 14 can be used as PWM outputs), 16 analog inputs, 4 UARTs (hardware serial ports), a 16 MHz crystal oscillator, a USB connection, a power jack, an ICSP header, and a reset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
