# Fritzing sketch 2.4 LED Bar Graph (saved by Fritzing 0.9.2b)
breadboards: 1

parts:
  元件1 = Arduino Mega ADK (Rev3)
  R10 = Resistor [tolerance=±5% resistance=220 package=THT]
  R4 = Resistor [tolerance=±5% resistance=220 package=THT]
  R7 = Resistor [tolerance=±5% resistance=220 package=THT]
  R3 = Resistor [tolerance=±5% resistance=220 package=THT]
  R1 = Resistor [tolerance=±5% resistance=220 package=THT]
  R8 = Resistor [tolerance=±5% resistance=220 package=THT]
  D1 = LED_BARGRAPH_10 [package=led_bargaph_10]
  R11 = Resistor [tolerance=±5% resistance=220 package=THT]
  R12 = Resistor [tolerance=±5% resistance=220 package=THT]
  R13 = Resistor [tolerance=±5% resistance=220 package=THT]
  R14 = Resistor [tolerance=±5% resistance=220 package=THT]

nets:
  N1: 元件1.GND, R10.Pin_1, R4.Pin_1, R7.Pin_1, R3.Pin_1, R1.Pin_1, R8.Pin_1, R11.Pin_1, R12.Pin_1, R13.Pin_1, R14.Pin_1
  N2: 元件1.D11_PWM, D1.A_A
  N3: 元件1.D10_PWM, D1.B_A
  N4: 元件1.D9_PWM, D1.C_A
  N5: 元件1.D8_PWM, D1.D_A
  N6: 元件1.D2_PWM, D1.J_A
  N7: 元件1.D3_PWM, D1.I_A
  N8: 元件1.D4_PWM, D1.H_A
  N9: 元件1.D5_PWM, D1.G_A
  N10: 元件1.D6_PWM, D1.F_A
  N11: 元件1.D7_PWM, D1.E_A
  N12: R10.Pin_0, D1.G_C
  N13: R4.Pin_0, D1.H_C
  N14: R7.Pin_0, D1.I_C
  N15: R3.Pin_0, D1.E_C
  N16: R1.Pin_0, D1.J_C
  N17: R8.Pin_0, D1.F_C
  N18: D1.D_C, R11.Pin_0
  N19: D1.C_C, R12.Pin_0
  N20: D1.B_C, R13.Pin_0
  N21: D1.A_C, R14.Pin_0

custom parts:
  Arduino Mega ADK (Rev3): The Arduino ADK is a microcontroller board based on the ATmega2560 (datasheet). It has a USB host interface to connect with Android based phones, based on the MAX3421e IC. It has 54 digital input/output pins (of which 14 can be used as PWM outputs), 16 analog inputs, 4 UARTs (hardware serial ports), a 16 MHz crystal oscillator, a USB connection, a power jack, an ICSP header, and a reset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
