# Fritzing sketch 2.5 7-Segment Display (saved by Fritzing 0.9.2b)
breadboards: 1

parts:
  元件1 = Arduino Mega ADK (Rev3)
  DI1 = 7-Segment LED Display [package=THT]
  R5 = Resistor [tolerance=±5% resistance=220 package=THT]
  R6 = Resistor [tolerance=±5% resistance=220 package=THT]
  R7 = Resistor [tolerance=±5% resistance=220 package=THT]
  R8 = Resistor [tolerance=±5% resistance=220 package=THT]
  R9 = Resistor [tolerance=±5% resistance=220 package=THT]
  R10 = Resistor [tolerance=±5% resistance=220 package=THT]
  R11 = Resistor [tolerance=±5% resistance=220 package=THT]
  R12 = Resistor [tolerance=±5% resistance=220 package=THT]

nets:
  N1: 元件1.GND, DI1.commAnode#2
  N2: 元件1.D11_PWM, R10.Pin_1
  N3: 元件1.D10_PWM, R9.Pin_1
  N4: 元件1.D9_PWM, R8.Pin_1
  N5: 元件1.D8_PWM, R7.Pin_1
  N6: 元件1.D4_PWM, R12.Pin_1
  N7: 元件1.D5_PWM, R11.Pin_1
  N8: 元件1.D6_PWM, R5.Pin_1
  N9: 元件1.D7_PWM, R6.Pin_1
  N10: DI1.cathodeE, R9.Pin_0
  N11: DI1.cathodeD, R10.Pin_0
  N12: DI1.cathodeC, R11.Pin_0
  N13: DI1.cathodeDP, R12.Pin_0
  N14: DI1.cathodeB, R5.Pin_0
  N15: DI1.cathodeA, R6.Pin_0
  N16: DI1.cathodeF, R7.Pin_0
  N17: DI1.cathodeG, R8.Pin_0

custom parts:
  Arduino Mega ADK (Rev3): The Arduino ADK is a microcontroller board based on the ATmega2560 (datasheet). It has a USB host interface to connect with Android based phones, based on the MAX3421e IC. It has 54 digital input/output pins (of which 14 can be used as PWM outputs), 16 analog inputs, 4 UARTs (hardware serial ports), a 16 MHz crystal oscillator, a USB connection, a power jack, an ICSP header, and a reset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
