# Fritzing sketch 2.8 MAX7219 (saved by Fritzing 0.9.2b)

parts:
  module1 = 1PCS MAX7219 LED Dot Matrix Module
  元件1 = Arduino Mega ADK (Rev3)

nets:
  VCC: module1.VCC, 元件1.5V
  GND: module1.GND, 元件1.GND
  N1: module1.DIN, 元件1.D12_PWM
  N2: module1.CS, 元件1.D10_PWM
  N3: module1.CLK, 元件1.D11_PWM

custom parts:
  Arduino Mega ADK (Rev3): The Arduino ADK is a microcontroller board based on the ATmega2560 (datasheet). It has a USB host interface to connect with Android based phones, based on the MAX3421e IC. It has 54 digital input/output pins (of which 14 can be used as PWM outputs), 16 analog inputs, 4 UARTs (hardware serial ports), a 16 MHz crystal oscillator, a USB connection, a power jack, an ICSP header, and a reset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
