# Fritzing sketch 3.1 Reversing Aid (saved by Fritzing 0.9.3b)
breadboards: 1

parts:
  元件1 = Arduino Mega ADK (Rev3)
  U1 = HC-SR04 [chip_label=IC package="SIP (Single Inline) [THT]"]
  S1 = buzzer [package="[THT]"]
  module1 = I2C LCD1602
  LED1 = LED - 5mm [color="Red (633nm)" package="5 mm [THT]"]
  R1 = Resistor [tolerance=±5% resistance=220 package=THT]

nets:
  N1: 元件1.D21/SCL, module1.SCL
  N2: 元件1.D20/SDA, module1.SDA
  GND: 元件1.GND, U1.GND, S1.GND, module1.GND, LED1.cathode
  N3: 元件1.D9_PWM, S1.VCC
  N4: 元件1.D8_PWM, R1.Pin_1
  VCC: 元件1.IOREF, 元件1.5V, U1.Vcc, module1.VCC
  N5: 元件1.D4_PWM, U1.Echo
  N6: 元件1.D5_PWM, U1.Trig
  N7: LED1.anode, R1.Pin_0

custom parts:
  Arduino Mega ADK (Rev3): The Arduino ADK is a microcontroller board based on the ATmega2560 (datasheet). It has a USB host interface to connect with Android based phones, based on the MAX3421e IC. It has 54 digital input/output pins (of which 14 can be used as PWM outputs), 16 analog inputs, 4 UARTs (hardware serial ports), a 16 MHz crystal oscillator, a USB connection, a power jack, an ICSP header, and a reset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
  HC-SR04: HC-SR04 ultrasound distance sensor
  I2C LCD1602: I2C LCD1602 module of SunFounder Sensor Kit
