# Fritzing sketch 3.2 Pedestrian Crossing Button (saved by Fritzing 0.9.3b)
breadboards: 1

parts:
  元件1 = Arduino Mega ADK (Rev3)
  U1 = 74HC595 [package="DIP16 [THT]"]
  DI1 = 7-Segment LED Display [package=THT]
  R6 = Resistor [tolerance=±5% resistance=220 package=THT]
  R8 = Resistor [tolerance=±5% resistance=220 package=THT]
  R10 = Resistor [tolerance=±5% resistance=220 package=THT]
  LED1 = LED - 5mm [color="Red (633nm)" package="5 mm [THT]"]
  LED2 = LED - 5mm [color="Green (560nm)" package="5 mm [THT]"]
  module1 = Touch Switch Module
  R11 = Resistor [tolerance=±5% resistance=220 package=THT]
  R12 = Resistor [tolerance=±5% resistance=220 package=THT]
  R13 = Resistor [tolerance=±5% resistance=220 package=THT]
  R14 = Resistor [tolerance=±5% resistance=220 package=THT]
  R15 = Resistor [tolerance=±5% resistance=220 package=THT]
  R16 = Resistor [tolerance=±5% resistance=220 package=THT]
  R17 = Resistor [tolerance=±5% resistance=220 package=THT]

nets:
  GND: 元件1.GND, U1.GND, U1.OE, DI1.commAnode#2, LED1.cathode, LED2.cathode, module1.GND
  N1: 元件1.D12_PWM, U1.ST_CP
  N2: 元件1.D11_PWM, U1.DS
  N3: 元件1.D8_PWM, U1.SH_CP
  VCC: 元件1.5V, U1.MR, U1.VCC, module1.VCC
  N4: 元件1.D2_PWM, module1.IO
  N5: 元件1.D5_PWM, R8.Pin_1
  N6: 元件1.D6_PWM, R6.Pin_1
  N7: U1.Q1, R17.Pin_1
  N8: U1.Q2, R12.Pin_1
  N9: U1.Q3, R14.Pin_1
  N10: U1.Q4, R10.Pin_1
  N11: U1.Q5, R11.Pin_1
  N12: U1.Q6, R13.Pin_1
  N13: U1.Q7, R15.Pin_1
  N14: U1.Q0, R16.Pin_1
  N15: DI1.cathodeE, R10.Pin_0
  N16: DI1.cathodeD, R14.Pin_0
  N17: DI1.cathodeC, R12.Pin_0
  N18: DI1.cathodeDP, R15.Pin_0
  N19: DI1.cathodeB, R17.Pin_0
  N20: DI1.cathodeA, R16.Pin_0
  N21: DI1.cathodeF, R11.Pin_0
  N22: DI1.cathodeG, R13.Pin_0
  N23: R6.Pin_0, LED2.anode
  N24: R8.Pin_0, LED1.anode

custom parts:
  Arduino Mega ADK (Rev3): The Arduino ADK is a microcontroller board based on the ATmega2560 (datasheet). It has a USB host interface to connect with Android based phones, based on the MAX3421e IC. It has 54 digital input/output pins (of which 14 can be used as PWM outputs), 16 analog inputs, 4 UARTs (hardware serial ports), a 16 MHz crystal oscillator, a USB connection, a power jack, an ICSP header, and a reset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
