# Fritzing sketch 3.3 Overheat Monitor (saved by Fritzing 0.9.2b)
breadboards: 1

parts:
  元件1 = Arduino Mega ADK (Rev3)
  module1 = I2C LCD1602
  module2 = 1PCS Rotary Encoder Module
  U1 = 1PCS Relay Module [package=relay-g5q]
  LED1 = LED - 5mm [color="Red (633nm)" package="5 mm [THT]"]
  S1 = Pushbutton [package="[THT]"]
  R2 = Resistor [tolerance=±5% resistance=220 package=THT]
  R3 = Temperature Sensor (Thermistor) [thermistor_type=NTC package=THT]  # not connected
  R4 = Temperature Sensor (Thermistor) [thermistor_type=NTC package=THT]
  R6 = Resistor [tolerance=±5% resistance=10k package=THT]
  R5 = Resistor [tolerance=±5% resistance=10k package=THT]

nets:
  N1: 元件1.A0, R4.pin_1, R6.Pin_0
  N2: 元件1.D21/SCL, module1.SCL
  N3: 元件1.D20/SDA, module1.SDA
  GND: 元件1.GND, module1.GND, module2.GND, U1.-, LED1.cathode, S1.Pin_3, S1.Pin_4
  N4: 元件1.D13_PWM, R2.Pin_1
  N5: 元件1.D10_PWM, S1.Pin_1, S1.Pin_2, R5.Pin_0
  VCC: 元件1.5V, module1.VCC, module2.VCC, U1.+, R4.pin_0, R5.Pin_1
  N6: 元件1.D2_PWM, U1.S
  N7: 元件1.D5_PWM, module2.SW
  N8: 元件1.D6_PWM, module2.DT
  N9: 元件1.D7_PWM, module2.CLK
  N10: LED1.anode, R2.Pin_0

custom parts:
  Arduino Mega ADK (Rev3): The Arduino ADK is a microcontroller board based on the ATmega2560 (datasheet). It has a USB host interface to connect with Android based phones, based on the MAX3421e IC. It has 54 digital input/output pins (of which 14 can be used as PWM outputs), 16 analog inputs, 4 UARTs (hardware serial ports), a 16 MHz crystal oscillator, a USB connection, a power jack, an ICSP header, and a reset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
  I2C LCD1602: I2C LCD1602 module of SunFounder Sensor Kit
  Pushbutton: A generic pushbutton.
