# Fritzing sketch 3.5 Access Control System (saved by Fritzing 0.9.3b)
breadboards: 1

parts:
  元件1 = Arduino Mega ADK (Rev3)
  IC1 = Power Module V1.0 [package=THT]
  module1 = I2C LCD1602
  IC2 = 4*4 keyboard [chip_label=IC package="DIP (Dual Inline) [THT]"]
  S1 = buzzer [package="[THT]"]
  module2 = RFID-RC522-blue
  U1 = Stepper Motor Driver-v1.0 [package="DIP28 [THT]"]
  module3 = Step Motor

nets:
  N1: 元件1.D21/SCL, module1.SDA
  N2: 元件1.D20/SDA, module1.SCL
  N3: 元件1.D12_PWM, S1.VCC
  N4: 元件1.D11_PWM, 元件1.D10_PWM, 元件1.D9_PWM, 元件1.D8_PWM, U1.IN1, U1.IN2, U1.IN3, U1.IN4
  3V3: 元件1.3V3, module2.3.3V
  5V: 元件1.5V, module1.VCC
  GND: 元件1.GND, IC1.-#5, module1.GND, S1.GND, module2.GND
  N5: 元件1.D2_PWM, module2.RST
  N6: 元件1.D3_PWM, module2.MISO
  N7: 元件1.D4_PWM, module2.MOSI
  N8: 元件1.D5_PWM, module2.SCK
  N9: 元件1.D6_PWM, module2.SDA
  N10: 元件1.D7_PWM, module2.IRQ
  N11: 元件1.D31, IC2.X1
  N12: 元件1.D33, IC2.X2
  N13: 元件1.D35, IC2.X3
  N14: 元件1.D37, IC2.X4
  N15: 元件1.D39, IC2.Y1
  N16: 元件1.D41, IC2.Y2
  N17: 元件1.D43, IC2.Y3
  N18: 元件1.D45, IC2.Y4
  N19: IC1.3.3V, IC1.-#4, U1.-
  N20: IC1.+#2, IC1.GND, U1.+
  N21: U1.OUT1, U1.OUT2, U1.OUT3, U1.OUT4, U1.COM, module3.yellow, module3.orange, module3.red, module3.pink, module3.blue

custom parts:
  Arduino Mega ADK (Rev3): The Arduino ADK is a microcontroller board based on the ATmega2560 (datasheet). It has a USB host interface to connect with Android based phones, based on the MAX3421e IC. It has 54 digital input/output pins (of which 14 can be used as PWM outputs), 16 analog inputs, 4 UARTs (hardware serial ports), a 16 MHz crystal oscillator, a USB connection, a power jack, an ICSP header, and a reset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
  Power Module V1.0: Power Module used for BreadBoard www.sunfounder.com
  I2C LCD1602: I2C LCD1602 module of SunFounder Sensor Kit
  4*4 keyboard: A 4*4 keyboard
  RFID-RC522-blue: RFID-RC522 module from Sunfounder
  Stepper Motor Driver-v1.0: Stepper Motor Driver
  Step Motor: step motor
