# Fritzing sketch 2.7 Tumbler (saved by Fritzing 0.9.3b)
breadboards: 1

parts:
  元件1 = Arduino Mega ADK (Rev3)
  R1 = Resistor [tolerance=±5% resistance=10k package=THT]
  IC1 = Tilt Switch [package="[THT]"]
  C1 = Capacitor [package=cap-pth-small2]

nets:
  N1: 元件1.GND, R1.Pin_0, C1.1
  N2: 元件1.D12_PWM, R1.Pin_1, IC1.pin1, C1.2
  N3: 元件1.5V, IC1.pin2

notes:
  104
  10K
  Tilt Switch
  Capacitor

custom parts:
  Arduino Mega ADK (Rev3): The Arduino ADK is a microcontroller board based on the ATmega2560 (datasheet). It has a USB host interface to connect with Android based phones, based on the MAX3421e IC. It has 54 digital input/output pins (of which 14 can be used as PWM outputs), 16 analog inputs, 4 UARTs (hardware serial ports), a 16 MHz crystal oscillator, a USB connection, a power jack, an ICSP header, and a reset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
  Tilt Switch: This is a ball tilt-switch with a metal ball inside. It is used to detect inclinations of a small angle.
  Capacitor: Capacitor Standard 0603 ceramic capacitor, and 0.1 leaded capacitor.
