# Fritzing sketch 2.9 light alarm (saved by Fritzing 0.9.3b)
breadboards: 1

parts:
  R2 = PHOTOCELL [package=photocell-kit]
  元件1 = Arduino Mega ADK (Rev3)
  R4 = Resistor [tolerance=±5% resistance=10k package=THT]

nets:
  N1: R2.P$1, 元件1.A0, R4.Pin_0
  N2: R2.P$2, 元件1.5V
  N3: 元件1.GND, R4.Pin_1

notes:
  10K
  Photoresistor

custom parts:
  Arduino Mega ADK (Rev3): The Arduino ADK is a microcontroller board based on the ATmega2560 (datasheet). It has a USB host interface to connect with Android based phones, based on the MAX3421e IC. It has 54 digital input/output pins (of which 14 can be used as PWM outputs), 16 analog inputs, 4 UARTs (hardware serial ports), a 16 MHz crystal oscillator, a USB connection, a power jack, an ICSP header, and a reset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
